# Fritzing sketch Untitled Sketch 2 (saved by Fritzing 0.9.6b)

parts:
  Mod1 = KY-028 Digital Temperature Sensor Module [package="Breakout board"]
  U1 = ESP32-38PinWide [part_number=ESP32-38PinWide]

nets:
  N1: Mod1.A0, U1.GPIO4
  N2: Mod1.G, U1.GND
  N3: Mod1.+, U1.3.3
  N4: Mod1.D0, U1.GPIO16

notes:
  3.3v ~ 5v

custom parts:
  KY-028 Digital Temperature Sensor Module: KY-028 Digital Temperature Sensor Module, used to measure changes in temperature.
  ESP32-38PinWide: Generic 38-Pin ESP32 with wide format (only access to one side of pins on a breadboard) based on Stephen Lilley's HiLetgo ESP-WROOM-32 ESP32 ESP-32S Development Board.
