# Fritzing sketch RotaryEncodersDiagram (saved by Fritzing 0.9.6b)

parts:
  U1 = ESP32-38PinWide [part_number=ESP32-38PinWide]
  RE1 = KY-040 Rotary encoder [package=THT]

nets:
  N1: U1.3.3, RE1.Vcc
  N2: U1.GPIO11, RE1.GND
  N3: U1.GPIO5, RE1.SW
  N4: U1.GPIO22, RE1.DT
  N5: U1.GPIO23, RE1.CLK

notes:
  3.3v ~ 5v

custom parts:
  ESP32-38PinWide: Generic 38-Pin ESP32 with wide format (only access to one side of pins on a breadboard) based on Stephen Lilley's HiLetgo ESP-WROOM-32 ESP32 ESP-32S Development Board.
  KY-040 Rotary encoder: KY-040 Rotary Encoder with switch on breakout borad from AZ Delivery
